# Fritzing sketch Sousduino (saved by Fritzing 0.9.2b)
circuit board: 5cm x 4.1cm
breadboards: 1

parts:
  R1 = Resistor [tolerance=±5% resistance=33k package=THT]
  R2 = Resistor [tolerance=±5% resistance=470 package=THT]
  R4 = Resistor [tolerance=±5% resistance=1k package=THT]
  R5 = Resistor [tolerance=±5% resistance=33k package=THT]
  Q1 = Basic FET N-Channel [part_number=TIC206 package="TO220 [THT]"]
  U5 = MOC3031-M [part_number=MOC3021 package=dil06]
  part = mystery part, 6 pins [chip_label=?]  # not connected
  J2 = screw terminal, 2 pins
  J3 = male pin header, 4 pins [form="♂ (male)"]
  U7 = Optocoupler [package=THT]
  R3 = Resistor [tolerance=±5% resistance=10k package=THT]
  Onderdeel1 = DB107
  J4 = screw terminal, 2 pins

nets:
  N1: R1.Pin_0, Onderdeel1.connector5
  N2: R1.Pin_1, R4.Pin_1, Q1.drain, J2.pin1
  N3: R2.Pin_0, J3.pin4
  N4: R2.Pin_1, U5.1
  N5: R4.Pin_0, U5.6
  N6: R5.Pin_0, Onderdeel1.connector0
  N7: R5.Pin_1, J2.pin2, J4.pin1
  N8: Q1.gate, U5.4
  N9: Q1.source, J4.pin2
  N10: U5.2, J3.pin3, U7.Pin_5
  N11: J3.pin1, R3.Pin_0
  N12: J3.pin2, U7.Pin_4, R3.Pin_1
  N13: U7.Pin_1, Onderdeel1.connector3
  N14: U7.Pin_2, Onderdeel1.connector2

notes:
  load
  Mains
  VCC
  ZERO
  GND
  SW
  -
  +
  MOC3021
  BTA41
  Bridge
  4N25
